// Logisim project reduce_equation.circ as structural Verilog: 1 circuit, main circuit main
module main (
  input  A,
  input  B,
  input  C,
  input  D
);

  wire and_1_out, and_2_out, not_1_out, not_2_out, not_3_out, or_1_out, or_2_out;

  not not_1 (not_1_out, A);
  not not_2 (not_2_out, C);
  not not_3 (not_3_out, D);
  or or_1 (or_1_out, B, not_3_out);
  and and_1 (and_1_out, not_1_out, not_2_out);
  and and_2 (and_2_out, and_1_out, or_1_out);
  or or_2 (or_2_out, A, and_2_out);
  LED led_1 (.in(or_2_out));
endmodule
