// Logisim project 2ram8x256.circ as structural Verilog: 1 circuit, main circuit main
module main (
  input  [15:0] Datos,
  input  [7:0] Direccion,
  input  in_3,
  input  in_4,
  input  in_5,
  input  in_6,
  output [15:0] out_7
);

  wire button_1_out;

  Button button_1 (.out(button_1_out));
  RAM #(.bus("separate")) ram_1 (
    .addr(Direccion), .din(Datos[7:0]), .data(out_7[7:0]), .str(in_3), .sel(in_4), .clk(button_1_out),
    .ld(in_5), .clr(in_6));
  RAM #(.bus("separate")) ram_2 (
    .addr(Direccion), .din(Datos[15:8]), .data(out_7[15:8]), .str(in_3), .sel(in_4), .clk(button_1_out),
    .ld(in_5), .clr(in_6));
endmodule
