// Logisim project ram8x256.circ as structural Verilog: 1 circuit, main circuit main
module main (
  input  [7:0] in_1,
  input  [15:0] in_2,
  input  in_3,
  input  in_4,
  input  in_5,
  input  in_6,
  output [15:0] out_7
);

  wire button_1_out;

  Button button_1 (.out(button_1_out));
  RAM #(.dataWidth(16), .bus("separate")) ram_1 (
    .addr(in_1), .din(in_2), .data(out_7), .str(in_3), .sel(in_4), .clk(button_1_out), .ld(in_5), .clr(in_6));
endmodule
