// Logisim project p2.circ as structural Verilog: 1 circuit, main circuit main
module main (
  input  [7:0] in_1,
  input  [3:0] _7,
  input  [3:0] _1,
  input  [3:0] _0,
  input  in_5,
  input  in_6,
  input  [3:0] in_7,
  output [7:0] out_8
);

  wire and_1_out, and_2_out, and_3_out, and_4_out, clock_1_out, decoder_1_out0, decoder_1_out1,
       decoder_1_out2, decoder_1_out3, decoder_1_out4, decoder_1_out5, decoder_1_out6, decoder_1_out7,
       decoder_1_out8, decoder_1_out9, decoder_1_out10, decoder_1_out11, decoder_1_out12, decoder_1_out13,
       decoder_1_out14, decoder_1_out15, not_1_out, not_2_out, not_3_out, not_4_out, not_5_out, not_6_out,
       not_7_out;
  wire [7:0] register_1_q;

  not not_1 (not_1_out, _7[0]);
  not not_2 (not_2_out, _7[1]);
  not not_3 (not_3_out, _1[0]);
  not not_4 (not_4_out, _7[2]);
  and and_1 (and_1_out, ~not_1_out, ~not_2_out, ~not_4_out, ~_7[3], ~not_3_out, ~_1[1], ~_1[2], ~_1[3], ~_0[0], ~_0[1], ~_0[2], ~_0[3]);  // AND_Gate
  not not_5 (not_5_out, and_1_out);
  and and_2 (and_2_out, ~not_5_out, ~not_6_out, ~in_6);  // AND_Gate
  Register #(.trigger("high")) register_1 (.D(in_1), .en(and_2_out), .Q(register_1_q), .clk(clock_1_out), .clr(in_5));
  Clock clock_1 (.out(clock_1_out));
  and and_3 (and_3_out, and_1_out, decoder_1_out3, in_6);
  assign out_8 = and_3_out ? register_1_q : 8'bz;  // Controlled_Buffer controlled_buffer_1
  not not_6 (not_6_out, and_4_out);
  and and_4 (and_4_out, ~decoder_1_out0, ~decoder_1_out1, ~not_7_out, ~decoder_1_out4, ~decoder_1_out5, ~decoder_1_out6, ~decoder_1_out7, ~decoder_1_out8, ~decoder_1_out9, ~decoder_1_out10, ~decoder_1_out11, ~decoder_1_out12, ~decoder_1_out13, ~decoder_1_out14, ~decoder_1_out15);  // AND_Gate
  not not_7 (not_7_out, decoder_1_out2);
  Decoder #(.select(4), .enable("false")) decoder_1 (
    .out0(decoder_1_out0), .out1(decoder_1_out1), .out2(decoder_1_out2), .out3(decoder_1_out3),
    .out4(decoder_1_out4), .out5(decoder_1_out5), .out6(decoder_1_out6), .out7(decoder_1_out7),
    .out8(decoder_1_out8), .out9(decoder_1_out9), .out10(decoder_1_out10), .out11(decoder_1_out11),
    .out12(decoder_1_out12), .out13(decoder_1_out13), .out14(decoder_1_out14), .out15(decoder_1_out15),
    .sel(in_7));
endmodule
