// Logisim project practica2.circ as structural Verilog: 1 circuit, main circuit main
module main (
  input  [7:0] in_1,
  input  in_2,
  input  _2,
  input  in_4,
  input  in_5,
  input  I_O,
  input  in_7,
  input  _0,
  input  in_9,
  input  in_10,
  input  in_11,
  input  in_12,
  input  _1,
  input  in_14,
  input  in_15,
  input  in_16,
  input  _7,
  input  in_18,
  input  in_19,
  input  in_20,
  input  _3,
  input  in_22,
  input  in_23,
  input  in_24,
  input  _0_2,
  input  in_26,
  input  in_27,
  input  in_28,
  input  _1_2,
  input  in_30,
  input  in_31,
  input  in_32,
  input  _7_2,
  input  in_34,
  input  in_35,
  output [7:0] out_36
);

  wire and_1_out, and_2_out, button_1_out, nand_1_out, nand_2_out, not_1_out, not_2_out, not_3_out,
       not_4_out, not_5_out, not_6_out, not_7_out, not_8_out, not_9_out, not_10_out, not_11_out;
  wire [7:0] register_1_q;

  not not_1 (not_1_out, _2);
  not not_2 (not_2_out, in_12);
  not not_3 (not_3_out, in_16);
  not not_4 (not_4_out, _7);
  not not_5 (not_5_out, in_18);
  not not_6 (not_6_out, in_20);
  not not_7 (not_7_out, _3);
  not not_8 (not_8_out, in_28);
  not not_9 (not_9_out, in_32);
  not not_10 (not_10_out, _7_2);
  not not_11 (not_11_out, in_34);
  nand nand_1 (nand_1_out, ~in_2, ~not_1_out, ~in_4, ~in_5, ~in_7, ~_0, ~in_9, ~in_11, ~not_2_out, ~_1, ~in_14, ~in_15, ~not_3_out, ~not_4_out, ~not_5_out, ~in_19);  // NAND_Gate
  nand nand_2 (nand_2_out, ~not_6_out, ~not_7_out, ~in_22, ~in_23, ~in_24, ~_0_2, ~in_26, ~in_27, ~not_8_out, ~_1_2, ~in_30, ~in_31, ~not_9_out, ~not_10_out, ~not_11_out, ~in_35);  // NAND_Gate
  and and_1 (and_1_out, ~nand_1_out, ~I_O);  // AND_Gate
  Button button_1 (.out(button_1_out));
  Register register_1 (.D(in_1), .en(and_1_out), .Q(register_1_q), .clk(button_1_out), .clr(in_10));
  and and_2 (and_2_out, I_O, ~nand_2_out);  // AND_Gate
  assign out_36 = and_2_out ? register_1_q : 8'bz;  // Controlled_Buffer controlled_buffer_1

  // Notes on the sheet:
  //   Matricula: 01217102
  //   Puerto de entrada: 7103
  //   Puerto de salida: 7102
endmodule
