// Logisim project practica3.circ as structural Verilog
module _8bitAdder1 (
  input  A1,
  input  A2,
  input  A3,
  input  A4,
  input  A5,
  input  A6,
  input  A7,
  input  A8,
  input  Carry,
  input  B1,
  input  B2,
  input  B3,
  input  B4,
  input  B5,
  input  B6,
  input  B7,
  input  B8,
  output out_18,
  output out_19,
  output out_20,
  output out_21,
  output out_22,
  output out_23,
  output out_24,
  output out_25,
  output out_26
);

  wire and_1_out, and_2_out, and_3_out, and_4_out, and_5_out, and_6_out, and_7_out, and_8_out, and_9_out,
       and_10_out, and_11_out, and_12_out, and_13_out, and_14_out, and_15_out, and_16_out, or_1_out,
       or_2_out, or_3_out, or_4_out, or_5_out, or_6_out, or_7_out, xor_1_out, xor_2_out, xor_3_out,
       xor_4_out, xor_5_out, xor_6_out, xor_7_out, xor_8_out;

  xor xor_1 (xor_1_out, A1, B1);
  xor xor_2 (xor_2_out, A2, B2);
  and and_1 (and_1_out, B1, A1);
  and and_2 (and_2_out, B2, A2);
  xor xor_3 (xor_3_out, A3, B3);
  and and_3 (and_3_out, B3, A3);
  xor xor_4 (xor_4_out, A4, B4);
  and and_4 (and_4_out, B4, A4);
  xor xor_5 (xor_5_out, A5, B5);
  and and_5 (and_5_out, B5, A5);
  xor xor_6 (xor_6_out, A6, B6);
  and and_6 (and_6_out, B6, A6);
  xor xor_7 (xor_7_out, A7, B7);
  xor xor_8 (xor_8_out, A8, B8);
  xor xor_9 (out_18, xor_1_out, Carry);
  and and_7 (and_7_out, Carry, xor_1_out);
  xor xor_10 (out_19, xor_2_out, or_1_out);
  and and_8 (and_8_out, or_1_out, xor_2_out);
  xor xor_11 (out_20, xor_3_out, or_2_out);
  and and_9 (and_9_out, or_2_out, xor_3_out);
  and and_10 (and_10_out, or_3_out, xor_4_out);
  and and_11 (and_11_out, B7, A7);
  and and_12 (and_12_out, B8, A8);
  xor xor_12 (out_21, xor_4_out, or_3_out);
  xor xor_13 (out_22, xor_5_out, or_4_out);
  and and_13 (and_13_out, or_4_out, xor_5_out);
  xor xor_14 (out_23, xor_6_out, or_5_out);
  and and_14 (and_14_out, or_5_out, xor_6_out);
  xor xor_15 (out_24, xor_7_out, or_6_out);
  and and_15 (and_15_out, or_6_out, xor_7_out);
  xor xor_16 (out_25, xor_8_out, or_7_out);
  and and_16 (and_16_out, or_7_out, xor_8_out);
  or or_1 (or_1_out, and_7_out, and_1_out);
  or or_2 (or_2_out, and_8_out, and_2_out);
  or or_3 (or_3_out, and_9_out, and_3_out);
  or or_4 (or_4_out, and_10_out, and_4_out);
  or or_5 (or_5_out, and_13_out, and_5_out);
  or or_6 (or_6_out, and_14_out, and_6_out);
  or or_7 (or_7_out, and_15_out, and_11_out);
  or or_8 (out_26, and_16_out, and_12_out);

  // Notes on the sheet:
  //   CarryOut
  //   CarryOut
  //   CarryOut
  //   CarryOut
  //   CarryOut
  //   CarryOut
  //   CarryOut
  //   CarryOut
endmodule

module _4bitAdder (
  input  A1,
  input  B1,
  input  CarryIn,
  input  A2,
  input  B2,
  input  A3,
  input  B3,
  input  A4,
  input  B4,
  output out_10,
  output out_11,
  output out_12,
  output out_13,
  output CarryOut
);

  wire and_1_out, and_2_out, and_3_out, and_4_out, and_5_out, and_6_out, and_7_out, and_8_out, or_1_out,
       or_2_out, or_3_out, xor_1_out, xor_2_out, xor_3_out, xor_4_out;

  xor xor_1 (xor_1_out, A1, B1);
  and and_1 (and_1_out, B1, A1);
  xor xor_2 (xor_2_out, A2, B2);
  and and_2 (and_2_out, B2, A2);
  xor xor_3 (xor_3_out, A3, B3);
  xor xor_4 (xor_4_out, A4, B4);
  and and_3 (and_3_out, B3, A3);
  and and_4 (and_4_out, B4, A4);
  xor xor_5 (out_10, xor_1_out, CarryIn);
  and and_5 (and_5_out, CarryIn, xor_1_out);
  xor xor_6 (out_11, xor_2_out, or_1_out);
  and and_6 (and_6_out, or_1_out, xor_2_out);
  xor xor_7 (out_12, xor_3_out, or_2_out);
  and and_7 (and_7_out, or_2_out, xor_3_out);
  xor xor_8 (out_13, xor_4_out, or_3_out);
  and and_8 (and_8_out, or_3_out, xor_4_out);
  or or_1 (or_1_out, and_5_out, and_1_out);
  or or_2 (or_2_out, and_6_out, and_2_out);
  or or_3 (or_3_out, and_7_out, and_3_out);
  or or_4 (CarryOut, and_8_out, and_4_out);

  // Notes on the sheet:
  //   CarryOut
  //   CarryOut
  //   CarryOut
  //   CarryOut
endmodule

module _8bitAdder2 (
  input  in_1,
  input  in_2,
  input  in_3,
  input  in_4,
  input  in_5,
  input  in_6,
  input  in_7,
  input  in_8,
  input  in_9,
  input  in_10,
  input  in_11,
  input  in_12,
  input  in_13,
  input  in_14,
  input  in_15,
  input  in_16,
  input  in_17,
  output out_18,
  output out_19,
  output out_20,
  output out_21,
  output out_22,
  output out_23,
  output out_24,
  output out_25
);

  wire n4bitadder_1_carryout;

  _4bitAdder u_4bitadder_1 (
    .A1(in_1), .B1(in_10), .CarryIn(in_2), .A2(in_3), .B2(in_11), .A3(in_4), .B3(in_12), .A4(in_5),
    .B4(in_13), .out_10(out_18), .out_11(out_19), .out_12(out_20), .out_13(out_21),
    .CarryOut(n4bitadder_1_carryout));
  _4bitAdder u_4bitadder_2 (
    .A1(in_6), .B1(in_14), .CarryIn(n4bitadder_1_carryout), .A2(in_7), .B2(in_15), .A3(in_8), .B3(in_16),
    .A4(in_9), .B4(in_17), .out_10(out_22), .out_11(out_23), .out_12(out_24), .out_13(out_25));  // open: CarryOut
endmodule
