// Logisim project practica3_1.circ as structural Verilog: 1 circuit, main circuit main
module main (
  input  Carry,
  input  [7:0] in_2,
  input  [7:0] in_3,
  input  [3:0] Instrucciones,
  input  Enable,
  input  [2:0] Shift_Amount,
  output [7:0] Output
);

  wire A_Carry, adder_1_cout, B_Carry, decoder_1_out0, decoder_1_out1, decoder_1_out2, decoder_1_out3,
       decoder_1_out4, decoder_1_out5, decoder_1_out6, decoder_1_out7, decoder_1_out8, decoder_1_out9,
       decoder_1_out10, decoder_1_out11, decoder_1_out12, decoder_1_out13, subtractor_1_bout;
  wire [7:0] adder_1_out, adder_2_out, adder_3_out, and_1_out, not_1_out, or_1_out, shifter_1_out,
       shifter_2_out, shifter_3_out, shifter_4_out, subtractor_1_out, subtractor_2_out, subtractor_3_out,
       xor_1_out;

  Decoder #(.select(4)) decoder_1 (
    .out0(decoder_1_out0), .out1(decoder_1_out1), .out2(decoder_1_out2), .out3(decoder_1_out3),
    .out4(decoder_1_out4), .out5(decoder_1_out5), .out6(decoder_1_out6), .out7(decoder_1_out7),
    .out8(decoder_1_out8), .out9(decoder_1_out9), .out10(decoder_1_out10), .out11(decoder_1_out11),
    .out12(decoder_1_out12), .out13(decoder_1_out13), .sel(Instrucciones), .en(Enable));  // open: out14, out15
  assign and_1_out = in_2 & in_3;  // AND_Gate and_1, 8 bits wide
  assign or_1_out = in_3 | in_2;  // OR_Gate or_1, 8 bits wide
  assign xor_1_out = in_3 ^ in_2;  // XOR_Gate xor_1, 8 bits wide
  assign not_1_out = ~in_2;  // NOT_Gate not_1, 8 bits wide
  Adder adder_1 (.a(in_3), .b(in_2), .out(adder_1_out), .cout(adder_1_cout));  // open: cin
  Adder adder_2 (.a(in_3), .b(in_2), .out(adder_2_out), .cin(adder_1_cout));  // open: cout
  Subtractor subtractor_1 (.a(in_3), .b(in_2), .out(subtractor_1_out), .bout(subtractor_1_bout));  // open: bin
  Subtractor subtractor_2 (.a(in_3), .b(in_2), .out(subtractor_2_out), .bin(subtractor_1_bout));  // open: bout
  Adder adder_3 (.a(in_2), .b(8'h1), .out(adder_3_out));  // open: cin, cout
  assign Output = decoder_1_out9 ? subtractor_3_out : 8'bz;  // Controlled_Buffer controlled_buffer_1
  Subtractor subtractor_3 (.a(in_2), .b(8'h1), .out(subtractor_3_out));  // open: bin, bout
  assign Output = decoder_1_out10 ? shifter_1_out : 8'bz;  // Controlled_Buffer controlled_buffer_2
  Shifter shifter_1 (.in(in_2), .\dist (Shift_Amount), .out(shifter_1_out));
  assign Output = decoder_1_out11 ? shifter_2_out : 8'bz;  // Controlled_Buffer controlled_buffer_3
  Shifter #(.shift("lr")) shifter_2 (.in(in_2), .\dist (Shift_Amount), .out(shifter_2_out));
  assign Output = decoder_1_out12 ? shifter_3_out : 8'bz;  // Controlled_Buffer controlled_buffer_4
  Shifter #(.shift("rl")) shifter_3 (.in(in_2), .\dist (Shift_Amount), .out(shifter_3_out));
  Shifter #(.shift("rr")) shifter_4 (.\dist (Shift_Amount), .out(shifter_4_out));  // open: in
  assign Output = decoder_1_out13 ? shifter_4_out : 8'bz;  // Controlled_Buffer controlled_buffer_5
  assign Output = decoder_1_out0 ? and_1_out : 8'bz;  // Controlled_Buffer controlled_buffer_6
  assign Output = decoder_1_out1 ? or_1_out : 8'bz;  // Controlled_Buffer controlled_buffer_7
  assign Output = decoder_1_out2 ? xor_1_out : 8'bz;  // Controlled_Buffer controlled_buffer_8
  assign Output = decoder_1_out3 ? not_1_out : 8'bz;  // Controlled_Buffer controlled_buffer_9
  assign Output = decoder_1_out4 ? adder_1_out : 8'bz;  // Controlled_Buffer controlled_buffer_10
  assign A_Carry = decoder_1_out4 ? adder_1_cout : 1'bz;  // Controlled_Buffer controlled_buffer_11
  assign Output = decoder_1_out5 ? adder_2_out : 8'bz;  // Controlled_Buffer controlled_buffer_12
  assign Output = decoder_1_out6 ? subtractor_1_out : 8'bz;  // Controlled_Buffer controlled_buffer_13
  assign B_Carry = decoder_1_out6 ? subtractor_1_bout : 1'bz;  // Controlled_Buffer controlled_buffer_14
  assign Output = decoder_1_out7 ? subtractor_2_out : 8'bz;  // Controlled_Buffer controlled_buffer_15
  assign Output = decoder_1_out8 ? adder_3_out : 8'bz;  // Controlled_Buffer controlled_buffer_16
  or or_2 (Carry, A_Carry, B_Carry);

  // Notes on the sheet:
  //   A
  //   B
  //   0000 - AND 
  //   0001 - OR
  //   0010 - XOR
  //   0011 - NOT A
  //   0100 - ADD
  //   0101 - ADC
  //   0110 -SUB B,A
  //   0111 - SBB B,A
  //   1000 INC A
  //   1001DEC A
  //   1010 SHL A
  //   1011 SHR A
  //   1100 - ROL A
  //   1101 ROR A
endmodule
